# Fritzing sketch WifiMic (saved by Fritzing 0.9.4)
circuit board: 7.43186cm x 5.08941cm
breadboards: 1

parts:
  R3 = Resistor [tolerance=±5% resistance=1k package="0603 [SMD]"]
  C4 = Ceramic Capacitor [capacitance=0.1µF package="0603 [SMD, multilayer]"]
  3_3v = V_REG_MIC2920 [package=sot223]
  PCM1803 = PCM1803 [package=ssop20]
  5_0v = V_REG_MIC2920 [package=sot223]
  24_576MHz = OSCILLATOR [package=crystal-smd-7.5x5.2-6pin]
  JP4 = Header 2 [package=molex-1x2_lock]
  MIC_IN = Header 2 [package=molex-1x2_lock]
  C5 = Electrolytic Capacitor [capacitance=1µF package="100 mil [THT, electrolytic]"]
  R5 = Resistor [tolerance=±5% resistance=220 package=THT]
  C6 = Electrolytic Capacitor [capacitance=1µF package="100 mil [THT, electrolytic]"]
  C8 = Ceramic Capacitor [capacitance=100nF package="100 mil [THT, multilayer]"]
  JP6 = Header 3 [package=molex-1x3_lock]
  POWER = Header 2 [package=molex-1x2_lock]
  C9 = Ceramic Capacitor [capacitance=100nF package="100 mil [THT, multilayer]"]
  R6 = Resistor [tolerance=±5% resistance=1k package="0603 [SMD]"]
  C10 = Ceramic Capacitor [capacitance=100nF package="100 mil [THT, multilayer]"]
  C11 = Ceramic Capacitor [capacitance=100nF package="100 mil [THT, multilayer]"]
  C12 = Ceramic Capacitor [capacitance=0.1µF package="0603 [SMD, multilayer]"]
  Pad1 = Pad [width=14.836817333333341 height=5.080024190476189 connect=center]  # not connected
  Pad2 = Pad [width=13.748233809523809 height=5.120321492063491 connect=center]  # not connected
  C3 = Ceramic Capacitor [capacitance=0.1µF package="0603 [SMD, multilayer]"]
  C13 = Ceramic Capacitor [capacitance=0.1µF package="0603 [SMD, multilayer]"]
  パーツ1 = ESP-WROOM-32 [ESP-32S] Module [part_number=ESP-WROOM-32]

nets:
  3.3V: R3.Pin_0, 3_3v.OUT, PCM1803.VDD, 24_576MHz.EN, 24_576MHz.VCC, R6.Pin_0, C10.1, C12.1, C13.1, パーツ1.3V3
  N1: R3.Pin_1, C3.1, パーツ1.EN
  GND: C4.0, 3_3v.GND, PCM1803.GNDA, PCM1803.GNDD, 5_0v.GND, 24_576MHz.GND, MIC_IN.2, C6.-, C8.0, JP6.3, POWER.2, C9.0, C10.0, C11.0, C12.0, C3.0, C13.0, パーツ1.GND, パーツ1.RST
  N2: C4.1, JP4.2, R6.Pin_1
  N3: 3_3v.IN, 5_0v.IN, POWER.1
  N4: PCM1803.VINL, PCM1803.VINR, R5.Pin_1, C6.+
  N5: PCM1803.VREF1, C8.1
  N6: PCM1803.VREF2, C9.1
  5V: PCM1803.VCCA, 5_0v.OUT, C11.1
  N7: PCM1803.LRCK, パーツ1.IO13
  N8: PCM1803.BCK, パーツ1.SD3
  N9: PCM1803.DOUT, パーツ1.SD2
  N10: PCM1803.SCK, 24_576MHz.OUT
  N11: JP4.1, パーツ1.IO0
  N12: MIC_IN.1, C5.-
  N13: C5.+, R5.Pin_0
  N14: JP6.1, パーツ1.RXD0
  N15: JP6.2, パーツ1.TXD0

notes:
  Write Enable
  Serial
  Power
  Mic In
  ESP-32 Wifi MIC
  ESP-WROOM-32
  B+
  B-
  signal
  GND
  ena
  serial
  R T G

custom parts:
  ESP-WROOM-32 [ESP-32S] Module: Espressif ESP-WROOM-32 WiFi/Bluetooth LE microcontroller module also known as the Ai-Thinker ESP-32S module with similar formfactor. The ESP32 is a microcontroller chip with WiFi and BLE capabilities. The chip is developed by Espressif and is the successor to the popular ESP8266 WiFi module.
